# Fritzing sketch two_relays_one_switch (saved by Fritzing 0.9.6b)
perfboards: 1

parts:
  OMRON1 = OMRON PCB Power Relay – G5LE [part_number="G5LE-1\n" package=THT]
  OMRON2 = OMRON PCB Power Relay – G5LE [part_number="G5LE-1\n" package=THT]
  J2 = Screw terminal - 2 pins [package=THT]
  J3 = Screw terminal - 2 pins [package=THT]

nets:
  N1: OMRON1.C, J2.pin2
  N2: OMRON1.B, OMRON2.B
  N3: OMRON2.C, J3.pin2
  N4: J2.pin1, J3.pin1

notes:
  - GRID
  + GRID
